// Logisim project DEMUX.circ as structural Verilog: 1 circuit, main circuit main
module main (
  input  S0,
  input  S1,
  input  Y
);

  wire and_1_out, and_2_out, and_3_out, and_4_out, not_1_out, not_2_out;

  not not_1 (not_1_out, S0);
  not not_2 (not_2_out, S1);
  and and_1 (and_1_out, not_2_out, not_1_out, not_1_out, Y);
  and and_2 (and_2_out, not_1_out, S1, Y);
  and and_3 (and_3_out, S0, not_2_out, Y);
  and and_4 (and_4_out, S0, S1, Y);
  LED led_1 (.in(and_1_out));
  LED led_2 (.in(and_2_out));
  LED led_3 (.in(and_3_out));
  LED led_4 (.in(and_4_out));

  // Notes on the sheet:
  //   1x4 DEMULTIPLEXER
  //   D0
  //   D1
  //   D2
  //   D3
endmodule
