// Logisim project FULL SUB.circ as structural Verilog: 1 circuit, main circuit main
module main (
  input  A,
  input  B,
  input  Cin,
  output D,
  output Bout
);

  wire and_1_out, and_2_out, not_1_out, not_2_out, xor_1_out;

  not not_1 (not_1_out, A);
  xor xor_1 (xor_1_out, A, B);
  not not_2 (not_2_out, xor_1_out);
  xor xor_2 (D, xor_1_out, Cin);
  and and_1 (and_1_out, not_2_out, Cin);
  and and_2 (and_2_out, not_1_out, B);
  or or_1 (Bout, and_1_out, and_2_out);

  // Notes on the sheet:
  //   FULL SUBTRACTOR
endmodule
