// Logisim project ripple.circ as structural Verilog: 1 circuit, main circuit main
module main (
  input  A0,
  input  B0,
  input  A1,
  input  B1,
  input  A2,
  input  B2,
  input  A3,
  input  B3,
  output S0,
  output S1,
  output S2,
  output S3,
  output C
);

  wire main_1_cout, main_2_cout, main_3_cout;

  full_adder_main main_1 (.A(A0), .B(B0), .Cin(1'b0), .Sum(S0), .Cout(main_1_cout));
  full_adder_main main_2 (.A(main_1_cout), .B(A1), .Cin(B1), .Sum(S1), .Cout(main_2_cout));
  full_adder_main main_3 (.A(main_2_cout), .B(A2), .Cin(B2), .Sum(S2), .Cout(main_3_cout));
  full_adder_main main_4 (.A(main_3_cout), .B(A3), .Cin(B3), .Sum(S3), .Cout(C));
endmodule
